// Logisim project Z80 - wersja_ostateczna.circ as structural Verilog: 7 circuits, main circuit main
module main (
);

  wire ALUEN, and_1_out, button_1_out, CzyJump, MEMWRITE, or_1_out, Write, Zegar;
  wire [2:0] RejestrH, RejestrL;
  wire [3:0] Operation;
  wire [5:0] CzyZmienicFlagi, Flagi, NoweFlagi;
  wire [7:0] ALUResult, controlled_buffer_1_out, controlled_buffer_3_out, Data, InputFromMemory,
       Instruction_data, multiplexer_1_out, RegOut1, RegOut2;
  wire [15:0] HL, JumpGdzie, PC_q;

  Clock clk (.out(Zegar));
  Button button_1 (.out(button_1_out));
  Counter #(.max('hffff), .width(16)) PC (
    .clr(button_1_out), .load(CzyJump), .clk(Zegar), .D(JumpGdzie), .Q(PC_q));  // open: up, count, carry
  FLAGS flags_1 (.Flag_input(NoweFlagi), .Flag_enable(CzyZmienicFlagi), .clk(Zegar), .Flag_output(Flagi));
  assign controlled_buffer_1_out = ALUEN ? ALUResult : 8'bz;  // Controlled_Buffer controlled_buffer_1
  assign controlled_buffer_1_out = Write ? Data : 8'bz;  // Controlled_Buffer controlled_buffer_2
  ROM #(.addrWidth(16)) Instruction (.addr(PC_q), .data(Instruction_data));
  RAM #(.addrWidth(16)) Memory (
    .addr(HL), .we(MEMWRITE), .oe(1'b1), .clk(Zegar), .din(controlled_buffer_1_out), .dout(InputFromMemory));
  assign controlled_buffer_3_out = ALUEN ? ALUResult : 8'bz;  // Controlled_Buffer controlled_buffer_3
  assign controlled_buffer_3_out = Write ? Data : 8'bz;  // Controlled_Buffer controlled_buffer_4
  or or_1 (or_1_out, ALUEN, Write);
  and and_1 (and_1_out, ~RejestrH[0], RejestrH[1], RejestrH[2]);  // AND_Gate
  MainRegisters mainregisters_1 (
    .DATA(controlled_buffer_3_out), .OUT1(RejestrH), .WRITE(or_1_out), .wybor_rejestru(RejestrH),
    .OUT2(RejestrL), .clk(Zegar), .WYJ1(RegOut1), .WYJ2(RegOut2), .HL(HL));
  Control_Unit control_unit_1 (
    .Instruction(Instruction_data), .Clock(Zegar), .DATA_Reg1(RegOut1), .DATA_Reg2(RegOut2),
    .DATA_ALU(ALUResult), .DATA_Memory(InputFromMemory), .DATA_Flags(Flagi), .RejestrH(RejestrH),
    .RejestrL(RejestrL), .Data(Data), .WriteRegister(Write), .ALU_Operation(Operation), .ALUOP(ALUEN),
    .MEMWRITE(MEMWRITE), .PerformJump(CzyJump), .JumpLokalizacja(JumpGdzie), .FlagEnable(CzyZmienicFlagi));
  Multiplexer #(.width(8)) multiplexer_1 (
    .in0(RegOut1), .in1(InputFromMemory), .out(multiplexer_1_out), .sel(and_1_out));
  ALU alu_1 (
    .WEJ1(multiplexer_1_out), .WEJ2(Data), .Operation(Operation), .CARRY(Flagi[0]), .ALOP(ALUEN),
    .Result(ALUResult), .FlagiOut(NoweFlagi));

  // Notes on the sheet:
  //   contents of Instruction (hex, n*v repeats v):
  //   3e 3 3d c2 2 0 3e 2 36 e 86 c6 4 47 cb 38 cb 38 b0
endmodule

module MainRegisters (
  input  [7:0] DATA,
  input  [2:0] OUT1,
  input  WRITE,
  input  [2:0] wybor_rejestru,
  input  [2:0] OUT2,
  input  clk,
  output [7:0] WYJ1,
  output [7:0] WYJ2,
  output [15:0] HL
);

  wire decoder_1_out0, decoder_1_out1, decoder_1_out2, decoder_1_out3, decoder_1_out4, decoder_1_out5,
       decoder_1_out7;
  wire [7:0] A_q, B_q, C_q, D_q, E_q;

  Decoder #(.select(3)) decoder_1 (
    .out0(decoder_1_out0), .out1(decoder_1_out1), .out2(decoder_1_out2), .out3(decoder_1_out3),
    .out4(decoder_1_out4), .out5(decoder_1_out5), .out7(decoder_1_out7), .sel(wybor_rejestru), .en(WRITE));  // open: out6
  Register A (.D(DATA), .en(decoder_1_out7), .clk(clk), .Q(A_q));  // open: clr
  Register B (.D(DATA), .en(decoder_1_out0), .clk(clk), .Q(B_q));  // open: clr
  Register D (.D(DATA), .en(decoder_1_out2), .clk(clk), .Q(D_q));  // open: clr
  Register H (.D(DATA), .en(decoder_1_out4), .clk(clk), .Q(HL[15:8]));  // open: clr
  Register C (.D(DATA), .en(decoder_1_out1), .clk(clk), .Q(C_q));  // open: clr
  Register E (.D(DATA), .en(decoder_1_out3), .clk(clk), .Q(E_q));  // open: clr
  Register L (.D(DATA), .en(decoder_1_out5), .clk(clk), .Q(HL[7:0]));  // open: clr
  Multiplexer #(.select(3), .width(8)) multiplexer_1 (
    .in0(B_q), .in1(C_q), .in2(D_q), .in3(E_q), .in4(HL[15:8]), .in5(HL[7:0]), .in7(A_q), .out(WYJ1),
    .sel(OUT1));  // open: in6
  Multiplexer #(.select(3), .width(8)) multiplexer_2 (
    .in0(B_q), .in1(C_q), .in2(D_q), .in3(E_q), .in4(HL[15:8]), .in5(HL[7:0]), .in7(A_q), .out(WYJ2),
    .sel(OUT2));  // open: in6

  // Notes on the sheet:
  //   111
  //   000
  //   010
  //   100
  //   001
  //   011
  //   101
endmodule

module ALU (
  input  [7:0] WEJ1,
  input  [7:0] WEJ2,
  input  [3:0] Operation,
  input  CARRY,
  input  ALOP,
  output [7:0] Result,
  output [5:0] FlagiOut
);

  wire and_2_out, and_3_out, and_4_out, even_parity_1_out, or_2_out, or_3_out;
  wire [0:0] demultiplexer_1_out10_2, demultiplexer_1_out11_2, demultiplexer_1_out12_2,
       demultiplexer_1_out13_2, demultiplexer_1_out14_2, demultiplexer_1_out15_2;
  wire [1:1] multiplexer_2_out;
  wire [2:0] customadder_1_hvc, customadder_2_hvc, customsub_1_hvc, customsub_2_hvc, customsub_3_hvc;
  wire [6:0] demultiplexer_1_out11, demultiplexer_1_out15, multiplexer_1_out;
  wire [7:0] and_1_out, customadder_1_dataout, customadder_2_dataout, customsub_1_dataout,
       customsub_2_dataout, customsub_3_dataout, demultiplexer_1_out0, demultiplexer_1_out1,
       demultiplexer_1_out2, demultiplexer_1_out3, demultiplexer_1_out4, demultiplexer_1_out5,
       demultiplexer_1_out6, demultiplexer_1_out7, demultiplexer_1_out8, demultiplexer_1_out9,
       demultiplexer_1_out13, demultiplexer_2_out0, demultiplexer_2_out1, demultiplexer_2_out2,
       demultiplexer_2_out3, demultiplexer_2_out4, demultiplexer_2_out5, demultiplexer_2_out6,
       demultiplexer_2_out7, or_1_out, xor_1_out;
  wire [7:1] demultiplexer_1_out10, demultiplexer_1_out12, demultiplexer_1_out14;

  Demultiplexer #(.enable("true"), .select(4), .width(8)) demultiplexer_1 (
    .out0(demultiplexer_1_out0), .out1(demultiplexer_1_out1), .out2(demultiplexer_1_out2),
    .out3(demultiplexer_1_out3), .out4(demultiplexer_1_out4), .out5(demultiplexer_1_out5),
    .out6(demultiplexer_1_out6), .out7(demultiplexer_1_out7),
    .out8({demultiplexer_1_out8[0], demultiplexer_1_out8[7:1]}),
    .out9({demultiplexer_1_out9[6:0], demultiplexer_1_out9[7]}),
    .out10({demultiplexer_1_out10_2[0], demultiplexer_1_out10}),
    .out11({demultiplexer_1_out11, demultiplexer_1_out11_2[0]}),
    .out12({demultiplexer_1_out12_2[0], demultiplexer_1_out12}),
    .out13({demultiplexer_1_out13[7], demultiplexer_1_out13[5:0], demultiplexer_1_out13_2[0]}),
    .out14({demultiplexer_1_out14_2[0], demultiplexer_1_out14}),
    .out15({demultiplexer_1_out15, demultiplexer_1_out15_2[0]}), .in(WEJ1), .sel(Operation), .en(ALOP));
  Demultiplexer #(.enable("true"), .select(4), .width(8)) demultiplexer_2 (
    .out0(demultiplexer_2_out0), .out1(demultiplexer_2_out1), .out2(demultiplexer_2_out2),
    .out3(demultiplexer_2_out3), .out4(demultiplexer_2_out4), .out5(demultiplexer_2_out5),
    .out6(demultiplexer_2_out6), .out7(demultiplexer_2_out7), .in(WEJ2), .sel(Operation), .en(ALOP));  // open: out8, out9, out10, out11, out12, out13, out14, out15
  CustomAdder customadder_1 (
    .DataA(demultiplexer_1_out0), .DataB(demultiplexer_2_out0), .DataOut(customadder_1_dataout),
    .HVC(customadder_1_hvc));  // open: CarryIn
  CustomAdder customadder_2 (
    .CarryIn(CARRY), .DataA(demultiplexer_1_out1), .DataB(demultiplexer_2_out1),
    .DataOut(customadder_2_dataout), .HVC(customadder_2_hvc));
  CustomSub customsub_1 (
    .DataA(demultiplexer_1_out2), .DataB(demultiplexer_2_out2), .DataOut(customsub_1_dataout),
    .HVC(customsub_1_hvc));  // open: CarryIn
  CustomSub customsub_2 (
    .CarryIn(CARRY), .DataA(demultiplexer_1_out3), .DataB(demultiplexer_2_out3),
    .DataOut(customsub_2_dataout), .HVC(customsub_2_hvc));
  assign and_1_out = demultiplexer_1_out4 & demultiplexer_2_out4;  // AND_Gate and_1, 8 bits wide
  assign xor_1_out = demultiplexer_1_out5 ^ demultiplexer_2_out5;  // XOR_Gate xor_1, 8 bits wide
  assign or_1_out = demultiplexer_1_out6 | demultiplexer_2_out6;  // OR_Gate or_1, 8 bits wide
  CustomSub customsub_3 (
    .DataA(demultiplexer_1_out7), .DataB(demultiplexer_2_out7), .DataOut(customsub_3_dataout),
    .HVC(customsub_3_hvc));  // open: CarryIn
  Multiplexer #(.enable("true"), .select(4), .width(8)) multiplexer_1 (
    .in0(customadder_1_dataout), .in1(customadder_2_dataout), .in2(customsub_1_dataout),
    .in3(customsub_2_dataout), .in4(and_1_out), .in5(xor_1_out), .in6(or_1_out), .in7(customsub_3_dataout),
    .in8(demultiplexer_1_out8), .in9(demultiplexer_1_out9), .in10({demultiplexer_1_out10, CARRY}),
    .in11({CARRY, demultiplexer_1_out11}), .in12({demultiplexer_1_out12, 1'b0}),
    .in13({{2{demultiplexer_1_out13[7]}}, demultiplexer_1_out13[5:0]}), .in14({demultiplexer_1_out14, 1'b0}),
    .in15({1'b0, demultiplexer_1_out15}), .out({FlagiOut[5], multiplexer_1_out}), .sel(Operation), .en(ALOP));
  Multiplexer #(.enable("true"), .select(4), .width(3)) multiplexer_2 (
    .in0(customadder_1_hvc), .in1(customadder_2_hvc), .in2(customsub_1_hvc), .in3(customsub_2_hvc),
    .in4(3'b100), .in5(3'b000), .in6(3'b000), .in7(customsub_3_hvc), .in8({2'b00, demultiplexer_1_out8[0]}),
    .in9({2'b00, demultiplexer_1_out9[7]}), .in10({2'b00, demultiplexer_1_out10_2[0]}),
    .in11({2'b00, demultiplexer_1_out11_2[0]}), .in12({2'b00, demultiplexer_1_out12_2[0]}),
    .in13({2'b00, demultiplexer_1_out13_2[0]}), .in14({2'b00, demultiplexer_1_out14_2[0]}),
    .in15({2'b00, demultiplexer_1_out15_2[0]}), .out({FlagiOut[3], multiplexer_2_out[1], FlagiOut[0]}),
    .sel(Operation));  // open: en
  nor nor_1 (FlagiOut[4], multiplexer_1_out[0], multiplexer_1_out[1], multiplexer_1_out[2], multiplexer_1_out[3], multiplexer_1_out[4], multiplexer_1_out[5], multiplexer_1_out[6], FlagiOut[5]);
  xnor even_parity_1 (even_parity_1_out, multiplexer_1_out[0], multiplexer_1_out[1], multiplexer_1_out[2], multiplexer_1_out[3], multiplexer_1_out[4], multiplexer_1_out[5], multiplexer_1_out[6], FlagiOut[5]);
  Multiplexer multiplexer_3 (.in0(even_parity_1_out), .in1(multiplexer_2_out[1]), .out(FlagiOut[2]), .sel(and_2_out));
  and and_2 (and_2_out, ~Operation[3], or_2_out);  // AND_Gate
  or or_2 (or_2_out, ~Operation[2], and_3_out);  // OR_Gate
  and and_3 (and_3_out, Operation[1], Operation[0]);
  and and_4 (and_4_out, ~Operation[3], Operation[2], Operation[1], Operation[0]);  // AND_Gate
  Multiplexer #(.width(8)) multiplexer_4 (
    .in0({FlagiOut[5], multiplexer_1_out}), .in1(WEJ1), .out(Result), .sel(and_4_out));
  and and_5 (FlagiOut[1], ~Operation[3], Operation[1], or_3_out);  // AND_Gate
  or or_3 (or_3_out, ~Operation[2], Operation[0]);  // OR_Gate

  // Notes on the sheet:
  //   Rotate Left Branch
  //   Rotate Right Branch
  //   Rotate Left Into Carry
  //   Rotate Right Into Carry
  //   Shift Left Arithmetic
  //   Shift Right Arithmetic
  //   Shift Left Logical
  //   Shift Right Logical
endmodule

module FLAGS (
  input  [5:0] Flag_input,
  input  [5:0] Flag_enable,
  input  clk,
  output [5:0] Flag_output
);

  Register #(.width(1)) S (.D(Flag_input[5]), .en(Flag_enable[5]), .clk(clk), .Q(Flag_output[5]));  // open: clr
  Register #(.width(1)) Z (.D(Flag_input[4]), .en(Flag_enable[4]), .clk(clk), .Q(Flag_output[4]));  // open: clr
  Register #(.width(1)) HC (.D(Flag_input[3]), .en(Flag_enable[3]), .clk(clk), .Q(Flag_output[3]));  // open: clr
  Register #(.width(1)) PV (.D(Flag_input[2]), .en(Flag_enable[2]), .clk(clk), .Q(Flag_output[2]));  // open: clr
  Register #(.width(1)) N (.D(Flag_input[1]), .en(Flag_enable[1]), .clk(clk), .Q(Flag_output[1]));  // open: clr
  Register #(.width(1)) C (.D(Flag_input[0]), .en(Flag_enable[0]), .clk(clk), .Q(Flag_output[0]));  // open: clr
endmodule

module Control_Unit (
  input  [7:0] Instruction,
  input  Clock,
  input  [7:0] DATA_Reg1,
  input  [7:0] DATA_Reg2,
  input  [7:0] DATA_ALU,
  input  [7:0] DATA_Memory,
  input  [5:0] DATA_Flags,
  output [2:0] RejestrH,
  output [2:0] RejestrL,
  output [7:0] Data,
  output WriteRegister,
  output [3:0] ALU_Operation,
  output ALUOP,
  output MEMWRITE,
  output PerformJump,
  output [15:0] JumpLokalizacja,
  output [5:0] FlagEnable
);

  wire ALU_out, ALUwithN_out, CBIsOn, CBMemory_out, DaneNatychmiastowe_out, ForceA_out, HLdlaINC_DEC_out,
       INC_DEC_out, JUMP_out, JUMPbezwarunkowy_out, LoadNtoR_out, LoadRtoR_out, multiplexer_6_out, or_1_out,
       or_2_out, or_3_out, or_4_out, or_5_out, ReadFromMemory_out, Shift_Rotate_out, WriteToMemory_out,
       xnor_1_out, xnor_2_out, xnor_3_out, xnor_4_out;
  wire [0:0] register_3_q_2;
  wire [1:0] register_3_q_3;
  wire [2:0] multiplexer_10_out;
  wire [3:0] multiplexer_7_out;
  wire [7:0] multiplexer_1_out, multiplexer_2_out, multiplexer_3_out, multiplexer_4_out, multiplexer_9_out;
  wire [7:6] register_3_q;

  and CBMemory (CBMemory_out, JumpLokalizacja[2], JumpLokalizacja[1], ~JumpLokalizacja[0], CBIsOn);  // AND_Gate
  // AND_Gate SET has open pins: in0=JumpLokalizacja[7], in1=JumpLokalizacja[6], in2=CBIsOn, out=open
  // AND_Gate RES has open pins: in0=JumpLokalizacja[7], in1=JumpLokalizacja[6], in2=CBIsOn, out=open
  // AND_Gate BIT has open pins: in0=JumpLokalizacja[7], in1=JumpLokalizacja[6], in2=CBIsOn, out=open
  and Shift_Rotate (Shift_Rotate_out, ~JumpLokalizacja[7], ~JumpLokalizacja[6], CBIsOn);  // AND_Gate
  Register register_1 (.D(multiplexer_1_out), .clk(Clock), .Q(JumpLokalizacja[15:8]));  // open: en, clr
  Multiplexer #(.width(8)) multiplexer_1 (
    .in0(Instruction), .in1({8{1'b0}}), .out(multiplexer_1_out), .sel(PerformJump));
  and CB (CBIsOn, register_3_q[7], register_3_q[6], ~register_3_q_3[1], ~register_3_q_3[0], register_3_q_2[0], ~RejestrL[2], RejestrL[1], RejestrL[0]);  // AND_Gate
  Register register_2 (.D(multiplexer_2_out), .clk(Clock), .Q(JumpLokalizacja[7:0]));  // open: en, clr
  Multiplexer #(.width(8)) multiplexer_2 (
    .in0(JumpLokalizacja[15:8]), .in1({8{1'b0}}), .out(multiplexer_2_out), .sel(or_2_out));
  Multiplexer #(.width(8)) multiplexer_3 (.in0(DATA_Reg2), .in1(DATA_Memory), .out(multiplexer_3_out), .sel(or_1_out));
  or or_1 (or_1_out, CBMemory_out, or_5_out);
  Multiplexer #(.width(8)) multiplexer_4 (
    .in0(multiplexer_3_out), .in1(JumpLokalizacja[7:0]), .out(multiplexer_4_out), .sel(DaneNatychmiastowe_out));
  Multiplexer #(.width(8)) multiplexer_5 (.in0(multiplexer_4_out), .in1(8'h1), .out(Data), .sel(INC_DEC_out));
  xnor xnor_1 (xnor_1_out, DATA_Flags[4], register_3_q_2[0]);
  xnor xnor_2 (xnor_2_out, DATA_Flags[0], register_3_q_2[0]);
  xnor xnor_3 (xnor_3_out, DATA_Flags[2], register_3_q_2[0]);
  xnor xnor_4 (xnor_4_out, DATA_Flags[5], register_3_q_2[0]);
  and HLdlaINC_DEC (HLdlaINC_DEC_out, ~register_3_q[7], ~register_3_q[6], register_3_q_3[1], register_3_q_3[0], ~register_3_q_2[0], RejestrL[2], ~RejestrL[1]);  // AND_Gate
  or DaneNatychmiastowe (DaneNatychmiastowe_out, ALUwithN_out, LoadNtoR_out);
  and JUMPbezwarunkowy (JUMPbezwarunkowy_out, register_3_q[7], register_3_q[6], ~register_3_q_3[1], ~register_3_q_3[0], ~register_3_q_2[0], ~RejestrL[2], RejestrL[1], RejestrL[0]);  // AND_Gate
  or or_2 (or_2_out, JUMPbezwarunkowy_out, JUMP_out);
  and JUMP (JUMP_out, register_3_q[7], register_3_q[6], ~RejestrL[2], RejestrL[1], ~RejestrL[0]);  // AND_Gate
  Multiplexer #(.select(2)) multiplexer_6 (
    .in0(xnor_1_out), .in1(xnor_2_out), .in2(xnor_3_out), .in3(xnor_4_out), .out(multiplexer_6_out),
    .sel(register_3_q_3));
  or or_3 (or_3_out, CBIsOn, DaneNatychmiastowe_out, or_2_out);
  and INC_DEC (INC_DEC_out, ~register_3_q[7], ~register_3_q[6], RejestrL[2], ~RejestrL[1]);  // AND_Gate
  or or_4 (or_4_out, multiplexer_6_out, JUMPbezwarunkowy_out);
  or or_5 (or_5_out, HLdlaINC_DEC_out, ReadFromMemory_out);
  and and_1 (PerformJump, or_2_out, or_4_out);
  and ReadFromMemory (ReadFromMemory_out, RejestrL[2], RejestrL[1], ~RejestrL[0]);  // AND_Gate
  or or_6 (MEMWRITE, CBMemory_out, WriteToMemory_out);
  and WriteToMemory (WriteToMemory_out, ~register_3_q[7], register_3_q_3[1], register_3_q_3[0], ~register_3_q_2[0]);  // AND_Gate
  Multiplexer #(.width(4)) multiplexer_7 (
    .in0({1'b0, register_3_q_3, register_3_q_2[0]}), .in1({1'b1, JumpLokalizacja[5:3]}),
    .out(multiplexer_7_out), .sel(Shift_Rotate_out));
  Multiplexer #(.width(4)) multiplexer_8 (
    .in0(multiplexer_7_out), .in1({2'b00, RejestrL[0], 1'b0}), .out(ALU_Operation), .sel(INC_DEC_out));
  and ALUwithN (ALUwithN_out, register_3_q[7], register_3_q[6], RejestrL[2], RejestrL[1], ~RejestrL[0]);  // AND_Gate
  and ALU (ALU_out, register_3_q[7], ~register_3_q[6]);  // AND_Gate
  or ALU_ON (ALUOP, Shift_Rotate_out, INC_DEC_out, ALUwithN_out, ALU_out);
  Multiplexer #(.width(8)) multiplexer_9 (
    .in0(JumpLokalizacja[7:0]), .in1({8{1'b0}}), .out(multiplexer_9_out), .sel(or_3_out));
  and LoadNtoR (LoadNtoR_out, ~register_3_q[7], ~register_3_q[6], RejestrL[2], RejestrL[1], ~RejestrL[0]);  // AND_Gate
  or ForceA (ForceA_out, ALUwithN_out, ALU_out);
  Register register_3 (
    .D(multiplexer_9_out), .clk(Clock), .Q({register_3_q, register_3_q_3, register_3_q_2[0], RejestrL}));  // open: en, clr
  and LoadRtoR (LoadRtoR_out, ~register_3_q[7], register_3_q[6]);  // AND_Gate
  or Load (WriteRegister, LoadNtoR_out, LoadRtoR_out);
  and and_2 (FlagEnable[0], ALUOP, ~INC_DEC_out);  // AND_Gate
  Multiplexer #(.width(3)) multiplexer_10 (
    .in0({register_3_q_3, register_3_q_2[0]}), .in1(3'b111), .out(multiplexer_10_out), .sel(ForceA_out));
  Multiplexer #(.width(3)) multiplexer_11 (
    .in0(multiplexer_10_out), .in1(JumpLokalizacja[2:0]), .out(RejestrH), .sel(CBIsOn));

  assign FlagEnable[5:1] = {5{ALUOP}};

  // Other names for the same wires on the sheet: ArgumentDwubajtowy[15:0] = JumpLokalizacja;
  //   JezeliJumpToWyczyscPrzerzutniki = PerformJump; RejestrCB[2:0] = JumpLokalizacja[2:0]
endmodule

module CustomAdder (
  input  CarryIn,
  input  [7:0] DataA,
  input  [7:0] DataB,
  output [7:0] DataOut,
  output [2:0] HVC
);

  wire adder_1_cout, adder_2_cout, adder_3_cout, adder_5_cout, adder_6_cout;

  Adder #(.width(1)) adder_1 (.a(DataA[0]), .b(DataB[0]), .out(DataOut[0]), .cin(CarryIn), .cout(adder_1_cout));
  Adder #(.width(1)) adder_2 (.a(DataA[1]), .b(DataB[1]), .out(DataOut[1]), .cin(adder_1_cout), .cout(adder_2_cout));
  Adder #(.width(1)) adder_3 (.a(DataA[2]), .b(DataB[2]), .out(DataOut[2]), .cin(adder_2_cout), .cout(adder_3_cout));
  Adder #(.width(1)) adder_4 (.a(DataA[3]), .b(DataB[3]), .out(DataOut[3]), .cin(adder_3_cout), .cout(HVC[2]));
  Adder #(.width(1)) adder_5 (.a(DataA[4]), .b(DataB[4]), .out(DataOut[4]), .cin(HVC[2]), .cout(adder_5_cout));
  Adder #(.width(1)) adder_6 (.a(DataA[5]), .b(DataB[5]), .out(DataOut[5]), .cin(adder_5_cout), .cout(adder_6_cout));
  Adder #(.width(1)) adder_7 (.a(DataA[6]), .b(DataB[6]), .out(DataOut[6]), .cin(adder_6_cout), .cout(HVC[1]));
  Adder #(.width(1)) adder_8 (.a(DataA[7]), .b(DataB[7]), .out(DataOut[7]), .cin(HVC[1]), .cout(HVC[0]));
endmodule

module CustomSub (
  input  CarryIn,
  input  [7:0] DataA,
  input  [7:0] DataB,
  output [7:0] DataOut,
  output [2:0] HVC
);

  wire subtractor_1_bout, subtractor_2_bout, subtractor_3_bout, subtractor_5_bout, subtractor_6_bout;

  Subtractor #(.width(1)) subtractor_1 (
    .a(DataA[0]), .b(DataB[0]), .out(DataOut[0]), .bin(CarryIn), .bout(subtractor_1_bout));
  Subtractor #(.width(1)) subtractor_2 (
    .a(DataA[1]), .b(DataB[1]), .out(DataOut[1]), .bin(subtractor_1_bout), .bout(subtractor_2_bout));
  Subtractor #(.width(1)) subtractor_3 (
    .a(DataA[2]), .b(DataB[2]), .out(DataOut[2]), .bin(subtractor_2_bout), .bout(subtractor_3_bout));
  Subtractor #(.width(1)) subtractor_4 (
    .a(DataA[3]), .b(DataB[3]), .out(DataOut[3]), .bin(subtractor_3_bout), .bout(HVC[2]));
  Subtractor #(.width(1)) subtractor_5 (
    .a(DataA[4]), .b(DataB[4]), .out(DataOut[4]), .bin(HVC[2]), .bout(subtractor_5_bout));
  Subtractor #(.width(1)) subtractor_6 (
    .a(DataA[5]), .b(DataB[5]), .out(DataOut[5]), .bin(subtractor_5_bout), .bout(subtractor_6_bout));
  Subtractor #(.width(1)) subtractor_7 (
    .a(DataA[6]), .b(DataB[6]), .out(DataOut[6]), .bin(subtractor_6_bout), .bout(HVC[1]));
  Subtractor #(.width(1)) subtractor_8 (.a(DataA[7]), .b(DataB[7]), .out(DataOut[7]), .bin(HVC[1]), .bout(HVC[0]));
endmodule
